// Logisim project cpu.circ as structural Verilog
module PC (
  output [31:0] instr
);

  wire clock;
  wire [23:0] nextPC, PC;

  Clock clock_1 (.out(clock));
  Register #(.width(24)) register_1 (.D(nextPC), .en(1'b1), .clk(clock), .Q(PC));  // open: clr
  Adder #(.width(24)) adder_1 (.a(PC), .b(24'h1), .out(nextPC));  // open: cin, cout
  RAM #(.addrWidth(24), .dataWidth(32), .enables("line")) Instruction_Memory (
    .addr(PC), .clk(clock), .dout(instr));  // open: we, din
endmodule

module ALU (
);

  Adder adder_1 ();  // open: a, b, out, cin, cout
  Subtractor subtractor_1 ();  // open: a, b, out, bin, bout
  Multiplier multiplier_1 ();  // open: a, b, out, cin, cout
  Divider divider_1 ();  // open: a, b, out, upper, rem
  Negator negator_1 ();  // open: in, out
  Shifter shifter_1 ();  // open: in, dist, out
  Shifter #(.shift("lr")) shifter_2 ();  // open: in, dist, out
  Shifter #(.shift("ar")) shifter_3 ();  // open: in, dist, out
endmodule
